# Fritzing sketch montage (saved by Fritzing 0.9.3b)
breadboards: 1

parts:
  Composant2 = Adafruit SGP30 Gas Sensor
  Composant3 = Arduino Uno (Rev3)

nets:
  VIN: Composant2.VIN, Composant3.VIN
  GND: Composant2.GND, Composant3.GND
  N1: Composant2.SCL, Composant3.A5/SCL
  N2: Composant2.SDA, Composant3.A4/SDA
